// Logisim project MIPS-logisim.circ as structural Verilog: 11 circuits, main circuit main
module main (
  input  in_1,
  input  in_2,
  input  in_3,
  input  in_4,
  input  in_5,
  input  in_6,
  input  in_7,
  output [31:0] out_8,
  output [31:0] out_9,
  output [31:0] out_10,
  output [31:0] out_11,
  output [31:0] out_12,
  output out_13
);

  wire alu_1_out_overflow, and_2_out, and_4_out, and_5_out, and_11_out, and_12_out, and_13_out, and_18_out,
       BrP_Br, BrPredictor_out, BrPredictor_result, BrPredictor_WE, clk_brp, comparator_1_eq,
       comparator_2_eq, comparator_3_eq, comparator_4_eq, Ex_Branch, Ex_Jump, Ex_Mem2Reg, Ex_MemWr, Ex_Nzero,
       Ex_RegWr, Ex_Zero, FlushEX, fwEx_flag, fwMem_flag, fwWB_RegWr, ID_ALUimm, ID_Branch, ID_ExtOp,
       ID_Jump, ID_Mem2Reg, ID_MemWr, ID_Nzero, ID_RegWr, inEx_Mem2Reg, inEx_MemWr, Mem_RegWr,
       mips_decoder_1_branch, mips_decoder_1_jump, mips_decoder_1_memwr, mips_decoder_1_regwr,
       multiplexer_3_out, n_FlushEX, n_FlushID, n_stall_EX, n_stall_ID, n_stall_IF, n_stall_MEM, n_stall_WB,
       not_1_out, not_2_out, not_3_out, not_11_out, or_2_out, RegDst, register_4_q, register_5_q,
       register_8_q, register_15_q, register_16_q, register_23_q, register_24_q, register_26_q,
       register_27_q, register_28_q, register_29_q, register_35_q, register_39_q, xor_1_out;
  wire [4:0] Ex_Rw, fwWB_Rw, ID_ALUctl, ID_Rw, Mem_Rw, register_22_q, register_34_q;
  wire [5:0] func;
  wire [7:0] bit_extender_1_out, bit_extender_3_out;
  wire [15:0] register_21_q;
  wire [15:6] ID_imm16;
  wire [25:0] Ex_nextpc;
  wire [25:16] ID_jmptar;
  wire [29:0] bit_extender_2_out, bit_extender_4_out, BrP_target, Ex_btarget, Ex_jtarget, ID_nextpc,
       IF_nextpc, Mem_target, multiplexer_1_out, multiplexer_4_out, multiplexer_5_out, PC_q, register_6_q,
       register_7_q, register_12_q;
  wire [31:0] Ex_ALUout, Ex_BusB, ext_mux_1_out_32, fwMem_ALUout, fwWB_data, ID_BusA, ID_BusB, inEx_BusB,
       Mem_BusW, multiplexer_7_out, multiplexer_8_out, multiplexer_12_out, ram_1_dout, reg32_1_out_ra,
       reg32_1_out_rb, register_19_q, register_37_q, register_38_q;
  wire [31:26] instr;

  Multiplexer #(.width(30)) multiplexer_1 (
    .in0(multiplexer_4_out), .in1(Mem_target), .out(multiplexer_1_out), .sel(FlushEX));
  Register #(.trigger("falling"), .width(30)) PC (
    .D(multiplexer_1_out), .en(n_stall_IF), .clk(clk_brp), .Q(PC_q), .clr(in_7));
  Register #(.trigger("falling"), .width(32)) register_1 (
    .D(Ex_ALUout), .clk(clk_brp), .Q(fwMem_ALUout));  // open: en, clr
  Register #(.trigger("falling"), .width(1)) register_2 (
    .D(Ex_Mem2Reg), .clk(clk_brp), .Q(inEx_Mem2Reg));  // open: en, clr
  Register #(.trigger("falling"), .width(5)) register_3 (.D(Ex_Rw), .clk(clk_brp), .Q(Mem_Rw));  // open: en, clr
  Register #(.trigger("falling"), .width(1)) register_4 (
    .D(Ex_Nzero), .clk(clk_brp), .Q(register_4_q));  // open: en, clr
  Register #(.trigger("falling"), .width(1)) register_5 (
    .D(Ex_Zero), .clk(clk_brp), .Q(register_5_q));  // open: en, clr
  Register #(.trigger("falling"), .width(30)) register_6 (
    .D(Ex_btarget), .clk(clk_brp), .Q(register_6_q));  // open: en, clr
  Register #(.trigger("falling"), .width(30)) register_7 (
    .D(Ex_jtarget), .clk(clk_brp), .Q(register_7_q));  // open: en, clr
  Register #(.trigger("falling"), .width(1)) register_8 (
    .D(Ex_Jump), .clk(clk_brp), .Q(register_8_q));  // open: en, clr
  Register #(.trigger("falling"), .width(1)) register_9 (
    .D(Ex_Branch), .clk(clk_brp), .Q(BrPredictor_WE));  // open: en, clr
  Multiplexer #(.width(5)) multiplexer_2 (.in0(ID_jmptar[20:16]), .in1(ID_imm16[15:11]), .out(ID_Rw), .sel(RegDst));
  not not_1 (not_1_out, register_5_q);
  Multiplexer multiplexer_3 (.in0(register_5_q), .in1(not_1_out), .out(multiplexer_3_out), .sel(register_4_q));
  mips_decoder mips_decoder_1 (
    .in_op(instr), .in_func(func), .RegWr(mips_decoder_1_regwr), .ALUsrc(ID_ALUimm), .RegDst(RegDst),
    .ExtOp(ID_ExtOp), .MemtoReg(ID_Mem2Reg), .MemWr(mips_decoder_1_memwr), .Branch(mips_decoder_1_branch),
    .Nzero(ID_Nzero), .Jump(mips_decoder_1_jump), .ALUctl(ID_ALUctl));  // open: Rtype
  Multiplexer #(.width(30)) multiplexer_4 (.in0(IF_nextpc), .in1(BrP_target), .out(multiplexer_4_out), .sel(BrP_Br));
  Register #(.trigger("falling"), .width(30)) register_10 (
    .D(IF_nextpc), .clk(clk_brp), .Q(ID_nextpc));  // open: en, clr
  Register #(.trigger("falling"), .width(32)) register_11 (
    .D(out_8), .clk(clk_brp), .Q({instr, ID_jmptar, ID_imm16, func}));  // open: en, clr
  Register #(.trigger("falling"), .width(30)) register_12 (
    .D({Ex_jtarget[29:26], Ex_nextpc}), .clk(clk_brp), .Q(register_12_q));  // open: en, clr
  Multiplexer #(.width(30)) multiplexer_5 (
    .in0(register_12_q), .in1(register_6_q), .out(multiplexer_5_out), .sel(BrPredictor_result));
  and and_1 (BrPredictor_result, multiplexer_3_out, BrPredictor_WE);
  reg32 reg32_1 (
    .clear(in_6), .in_Ra(ID_jmptar[25:21]), .in_Rb(ID_jmptar[20:16]), .in_Rw(fwWB_Rw), .in_WE(fwWB_RegWr),
    .in_Rwdata(fwWB_data), .clk(clk_brp), .out_Ra(reg32_1_out_ra), .out_Rb(reg32_1_out_rb));
  xor xor_1 (xor_1_out, BrPredictor_result, BrPredictor_out);
  Register #(.trigger("falling"), .width(32)) register_13 (.D(Ex_BusB), .clk(clk_brp), .Q(inEx_BusB));  // open: en, clr
  Register #(.trigger("falling"), .width(1)) register_14 (
    .D(Ex_MemWr), .clk(clk_brp), .Q(inEx_MemWr));  // open: en, clr
  Register #(.trigger("falling"), .width(1)) register_15 (
    .D(Ex_RegWr), .clk(clk_brp), .Q(register_15_q));  // open: en, clr
  Register #(.trigger("falling"), .width(1)) register_16 (
    .D(out_13), .clk(clk_brp), .Q(register_16_q));  // open: en, clr
  and and_2 (and_2_out, BrPredictor_WE, xor_1_out);
  Adder #(.width(30)) adder_1 (.a(30'h1), .b(PC_q), .out(IF_nextpc));  // open: cin, cout
  Bit_Extender #(.in_width(30), .out_width(8)) bit_extender_1 (.in(PC_q), .out(bit_extender_1_out));
  and and_3 (ID_RegWr, mips_decoder_1_regwr, n_FlushID);
  Comparator #(.mode("unsigned"), .width(5)) comparator_1 (
    .a(ID_jmptar[25:21]), .b(Mem_Rw), .eq(comparator_1_eq));  // open: gt, lt
  Comparator #(.mode("unsigned"), .width(5)) comparator_2 (
    .a(Mem_Rw), .b(ID_jmptar[20:16]), .eq(comparator_2_eq));  // open: gt, lt
  Multiplexer #(.width(30)) multiplexer_6 (
    .in0(multiplexer_5_out), .in1(register_7_q), .out(Mem_target), .sel(register_8_q));
  RAM #(.asyncread("true"), .dataWidth(32), .trigger("falling")) ram_1 (
    .addr(bit_extender_1_out), .dout(ram_1_dout));  // open: we, oe, clk, din
  and and_4 (and_4_out, comparator_1_eq, fwMem_flag);
  and and_5 (and_5_out, fwMem_flag, comparator_2_eq);
  and and_6 (Mem_RegWr, register_15_q, not_2_out);
  not not_2 (not_2_out, register_16_q);
  or or_1 (FlushEX, register_8_q, and_2_out);
  Multiplexer #(.width(32)) multiplexer_7 (
    .in0(reg32_1_out_ra), .in1(fwMem_ALUout), .out(multiplexer_7_out), .sel(and_4_out));
  Multiplexer #(.width(32)) multiplexer_8 (
    .in0(reg32_1_out_rb), .in1(fwMem_ALUout), .out(multiplexer_8_out), .sel(and_5_out));
  and and_7 (ID_MemWr, mips_decoder_1_memwr, n_FlushID);
  Comparator #(.mode("unsigned"), .width(5)) comparator_3 (
    .a(ID_jmptar[25:21]), .b(Ex_Rw), .eq(comparator_3_eq));  // open: gt, lt
  Comparator #(.mode("unsigned"), .width(5)) comparator_4 (
    .a(Ex_Rw), .b(ID_jmptar[20:16]), .eq(comparator_4_eq));  // open: gt, lt
  assign bit_extender_2_out = {{14{ID_imm16[15]}}, {ID_imm16, func}};  // Bit_Extender bit_extender_2
  and and_8 (BrP_Br, ID_Branch, BrPredictor_out);
  Adder #(.width(30)) adder_2 (.a(ID_nextpc), .b(bit_extender_2_out), .out(BrP_target));  // open: cin, cout
  and and_9 (ID_Branch, mips_decoder_1_branch, n_FlushID);
  and and_10 (ID_Jump, mips_decoder_1_jump, n_FlushID);
  Multiplexer #(.width(32)) multiplexer_9 (.in0(multiplexer_7_out), .in1(Ex_ALUout), .out(ID_BusA), .sel(and_11_out));
  and and_11 (and_11_out, comparator_3_eq, fwEx_flag);
  and and_12 (and_12_out, fwEx_flag, comparator_4_eq);
  Multiplexer #(.width(32)) multiplexer_10 (.in0(multiplexer_8_out), .in1(Ex_ALUout), .out(ID_BusB), .sel(and_12_out));
  Multiplexer #(.width(32)) multiplexer_11 (.in0(ram_1_dout), .in1({32{1'b0}}), .out(out_8), .sel(or_2_out));
  or or_2 (or_2_out, BrP_Br, FlushEX);
  Bit_Extender #(.in_width(32), .out_width(8), .\type ("zero")) bit_extender_3 (
    .in(Ex_ALUout), .out(bit_extender_3_out));
  not not_3 (not_3_out, Ex_Mem2Reg);
  Clock clock_1 (.out(clk_brp));
  RAM #(.dataWidth(32), .trigger("falling")) ram_2 (
    .addr(bit_extender_3_out), .we(Ex_MemWr), .clk(clk_brp), .din(Ex_BusB), .dout(Mem_BusW));  // open: oe
  Register #(.trigger("falling"), .width(1)) register_17 (
    .D(and_13_out), .clk(clk_brp), .Q(fwMem_flag));  // open: en, clr
  and and_13 (and_13_out, Ex_RegWr, not_3_out);
  not not_4 (n_FlushID, FlushEX);
  not not_5 (n_FlushEX, FlushEX);
  Register #(.trigger("falling"), .width(30)) register_18 (
    .D(ID_nextpc), .clk(clk_brp), .Q({Ex_jtarget[29:26], Ex_nextpc}));  // open: en, clr
  Register #(.trigger("falling"), .width(32)) register_19 (
    .D(ID_BusA), .clk(clk_brp), .Q(register_19_q));  // open: en, clr
  Register #(.trigger("falling"), .width(32)) register_20 (.D(ID_BusB), .clk(clk_brp), .Q(Ex_BusB));  // open: en, clr
  Register #(.trigger("falling"), .width(16)) register_21 (
    .D({ID_imm16, func}), .clk(clk_brp), .Q(register_21_q));  // open: en, clr
  Register #(.trigger("falling"), .width(5)) register_22 (
    .D(ID_ALUctl), .clk(clk_brp), .Q(register_22_q));  // open: en, clr
  Register #(.trigger("falling"), .width(1)) register_23 (
    .D(ID_RegWr), .clk(clk_brp), .Q(register_23_q));  // open: en, clr
  Register #(.trigger("falling"), .width(1)) register_24 (
    .D(ID_MemWr), .clk(clk_brp), .Q(register_24_q));  // open: en, clr
  not not_6 (n_stall_IF, in_1);
  not not_7 (n_stall_ID, in_2);
  not not_8 (n_stall_EX, in_3);
  not not_9 (n_stall_MEM, in_4);
  not not_10 (n_stall_WB, in_5);
  Register #(.trigger("falling"), .width(26)) register_25 (
    .D({ID_jmptar, ID_imm16, func}), .clk(clk_brp), .Q(Ex_jtarget[25:0]));  // open: en, clr
  Register #(.trigger("falling"), .width(1)) register_26 (
    .D(ID_Jump), .clk(clk_brp), .Q(register_26_q));  // open: en, clr
  Register #(.trigger("falling"), .width(1)) register_27 (
    .D(ID_Branch), .clk(clk_brp), .Q(register_27_q));  // open: en, clr
  Register #(.trigger("falling"), .width(1)) register_28 (
    .D(ID_ExtOp), .clk(clk_brp), .Q(register_28_q));  // open: en, clr
  Register #(.trigger("falling"), .width(1)) register_29 (
    .D(ID_ALUimm), .clk(clk_brp), .Q(register_29_q));  // open: en, clr
  and and_14 (Ex_RegWr, register_23_q, n_FlushEX);
  and and_15 (Ex_MemWr, register_24_q, n_FlushEX);
  and and_16 (Ex_Jump, register_26_q, n_FlushEX);
  and and_17 (Ex_Branch, register_27_q, n_FlushEX);
  assign bit_extender_4_out = {{14{register_21_q[15]}}, register_21_q};  // Bit_Extender bit_extender_4
  Adder #(.width(30)) adder_3 (
    .a({Ex_jtarget[29:26], Ex_nextpc}), .b(bit_extender_4_out), .out(Ex_btarget));  // open: cin, cout
  ext_mux ext_mux_1 (.in_16(register_21_q), .ext_op(register_28_q), .out_32(ext_mux_1_out_32));
  and and_18 (and_18_out, ID_RegWr, not_11_out);
  not not_11 (not_11_out, ID_Mem2Reg);
  Register #(.trigger("falling"), .width(32)) register_30 (.D(out_8), .clk(clk_brp), .Q(out_9));  // open: en, clr
  Register #(.trigger("falling"), .width(32)) register_31 (.D(out_9), .clk(clk_brp), .Q(out_10));  // open: en, clr
  Register #(.trigger("falling"), .width(32)) register_32 (.D(out_10), .clk(clk_brp), .Q(out_11));  // open: en, clr
  Register #(.trigger("falling"), .width(32)) register_33 (.D(out_11), .clk(clk_brp), .Q(out_12));  // open: en, clr
  Multiplexer #(.width(32)) multiplexer_12 (
    .in0(Ex_BusB), .in1(ext_mux_1_out_32), .out(multiplexer_12_out), .sel(register_29_q));
  Register #(.trigger("falling"), .width(5)) register_34 (
    .D(ID_imm16[10:6]), .clk(clk_brp), .Q(register_34_q));  // open: en, clr
  Register #(.trigger("falling"), .width(1)) register_35 (
    .D(and_18_out), .clk(clk_brp), .Q(register_35_q));  // open: en, clr
  Register #(.trigger("falling"), .width(1)) register_36 (
    .D(ID_Mem2Reg), .clk(clk_brp), .Q(Ex_Mem2Reg));  // open: en, clr
  and and_19 (fwEx_flag, register_35_q, n_FlushEX);
  ALU alu_1 (
    .in_A(register_19_q), .in_B(multiplexer_12_out), .ALUctr(register_22_q), .in_shamt(register_34_q),
    .out_Zero(Ex_Zero), .out_Overflow(alu_1_out_overflow), .out_Result(Ex_ALUout));
  Register #(.trigger("falling"), .width(32)) register_37 (
    .D(fwMem_ALUout), .clk(clk_brp), .Q(register_37_q));  // open: en, clr
  Register #(.trigger("falling"), .width(32)) register_38 (
    .D(Mem_BusW), .clk(clk_brp), .Q(register_38_q));  // open: en, clr
  Register #(.trigger("falling"), .width(1)) register_39 (
    .D(inEx_Mem2Reg), .clk(clk_brp), .Q(register_39_q));  // open: en, clr
  Register #(.trigger("falling"), .width(1)) register_40 (
    .D(Mem_RegWr), .clk(clk_brp), .Q(fwWB_RegWr));  // open: en, clr
  Register #(.trigger("falling"), .width(5)) register_41 (.D(Mem_Rw), .clk(clk_brp), .Q(fwWB_Rw));  // open: en, clr
  branch_predictor branch_predictor_1 (
    .result(BrPredictor_result), .WE(BrPredictor_WE), .clk(clk_brp), .clr(in_6), .prediction(BrPredictor_out));
  and and_20 (out_13, alu_1_out_overflow, n_FlushEX);
  Register #(.trigger("falling"), .width(5)) register_42 (.D(ID_Rw), .clk(clk_brp), .Q(Ex_Rw));  // open: en, clr
  Register #(.trigger("falling"), .width(1)) register_43 (.D(ID_Nzero), .clk(clk_brp), .Q(Ex_Nzero));  // open: en, clr
  Multiplexer #(.width(32)) multiplexer_13 (
    .in0(register_37_q), .in1(register_38_q), .out(fwWB_data), .sel(register_39_q));

  // Other names for the same wires on the sheet: clk_ex = clk_brp; clk_id = clk_brp; clk_if = clk_brp;
  //   clk_mem = clk_brp; clk_wr = clk_brp; clr = in_6; clr_pc = in_7; Ex_instr[31:0] = out_10;
  //   Ex_nextpc[29:26] = Ex_jtarget[29:26]; Ex_Overflow = out_13; FlushIF0 = BrP_Br; fwEx_ALUout[31:0] = Ex_ALUout;
  //   ID_instr[31:0] = out_9; IF_instr[31:0] = out_8; inEx_ALUout[31:0] = fwMem_ALUout;
  //   Mem_ALUout[31:0] = fwMem_ALUout; Mem_Mem2Reg = inEx_Mem2Reg; ID_imm16[5:0] = func;
  //   ID_jmptar[15:0] = {ID_imm16, func}; instr[25:0] = {ID_jmptar, ID_imm16, func}; ID_shamt[4:0] = ID_imm16[10:6];
  //   Rd[4:0] = ID_imm16[15:11]; Rt[4:0] = ID_jmptar[20:16]; Rs[4:0] = ID_jmptar[25:21]; Op[5:0] = instr;
  //   FlushID = FlushEX; FlushIF1 = FlushEX; Mem_Br = FlushEX; Mem_instr[31:0] = out_11; stall_EX = in_3;
  //   stall_ID = in_2; stall_IF = in_1; stall_MEM = in_4; stall_WB = in_5; Wr_instr[31:0] = out_12
endmodule

module mips_decoder (
  input  [5:0] in_op,
  input  [5:0] in_func,
  output Rtype,
  output RegWr,
  output ALUsrc,
  output RegDst,
  output ExtOp,
  output MemtoReg,
  output MemWr,
  output Branch,
  output Nzero,
  output Jump,
  output [4:0] ALUctl
);

  wire addiu_out, beq_out, not_1_out, not_2_out, not_3_out, not_4_out, not_5_out, not_6_out, not_7_out,
       not_8_out, not_9_out, not_10_out, not_11_out, not_12_out, not_13_out, not_14_out, not_15_out,
       not_16_out, not_17_out, not_18_out, not_19_out, not_20_out, not_21_out, not_22_out, not_23_out,
       not_24_out, not_25_out, not_26_out, not_27_out, not_28_out, not_29_out, not_30_out, not_31_out,
       not_32_out, not_33_out, not_34_out, not_35_out, not_36_out, not_37_out, not_38_out, not_39_out,
       not_40_out, not_41_out, not_42_out, not_43_out, not_44_out, not_45_out, not_46_out, not_47_out,
       not_48_out, not_49_out, not_50_out, not_51_out, not_52_out, not_53_out, op_addi_out, op_andi_out,
       op_lui_out, op_slti_out, op_sltiu_out, op_xori_out, or_5_out, ori_out;
  wire [3:0] or_1_out;
  wire [4:0] func2ALUop_out;

  PLA #(.in_width(6), .out_width(5), .\table ("100000 00001 # add\n100010 00101 # sub\n100011 00100 # subu\n101010 00111 # slt\n101011 00110 # sltu\n000000 00011 # sll\n100101 00010 # or\n100001 00000 # addu\n100100 01001 # and\n100110 01010 # xor\n000100 01011 # sllv\n100111 01101 # nor\n000011 01110 # sra\n000110 01111 # srlv\n000111 10000 # srav\n000010 01000 # srl")) func2ALUop (
    .in(in_func), .out(func2ALUop_out));
  Multiplexer #(.width(5)) multiplexer_1 (.in0({1'b0, or_1_out}), .in1(func2ALUop_out), .out(ALUctl), .sel(RegDst));
  or or_1 (or_1_out[0], addiu_out, op_andi_out, op_slti_out);
  or or_2 (or_1_out[1], op_xori_out, ori_out, op_sltiu_out, op_slti_out);
  or or_3 (or_1_out[2], beq_out, op_sltiu_out, Nzero, op_slti_out, op_lui_out);
  or or_4 (or_1_out[3], op_andi_out, op_xori_out, op_lui_out);
  not not_1 (not_1_out, in_op[5]);
  not not_2 (not_2_out, in_op[4]);
  not not_3 (not_3_out, in_op[3]);
  not not_4 (not_4_out, in_op[2]);
  not not_5 (not_5_out, in_op[1]);
  not not_6 (not_6_out, in_op[0]);
  and R_ty (RegDst, not_1_out, not_2_out, not_3_out, not_4_out, not_5_out, not_6_out);
  not not_7 (not_7_out, in_op[5]);
  not not_8 (not_8_out, in_op[4]);
  and ori (ori_out, not_7_out, not_8_out, in_op[3], in_op[2], not_10_out, in_op[0]);
  not not_9 (not_9_out, in_op[5]);
  not not_10 (not_10_out, in_op[1]);
  not not_11 (not_11_out, in_op[4]);
  not not_12 (not_12_out, in_op[1]);
  not not_13 (not_13_out, in_op[0]);
  and op_andi (op_andi_out, not_9_out, not_11_out, in_op[3], in_op[2], not_12_out, not_13_out);
  not not_14 (not_14_out, in_op[5]);
  not not_15 (not_15_out, in_op[4]);
  and op_xori (op_xori_out, not_14_out, not_15_out, in_op[3], in_op[2], in_op[1], not_16_out);
  not not_16 (not_16_out, in_op[0]);
  not not_17 (not_17_out, in_op[5]);
  not not_18 (not_18_out, in_op[4]);
  not not_19 (not_19_out, in_op[2]);
  not not_20 (not_20_out, in_op[1]);
  and addiu (addiu_out, not_17_out, not_18_out, in_op[3], not_19_out, not_20_out, in_op[0]);
  not not_21 (not_21_out, in_op[5]);
  not not_22 (not_22_out, in_op[4]);
  not not_23 (not_23_out, in_op[2]);
  not not_24 (not_24_out, in_op[1]);
  not not_25 (not_25_out, in_op[0]);
  and op_addi (op_addi_out, not_21_out, not_22_out, in_op[3], not_23_out, not_24_out, not_25_out);
  not not_26 (not_26_out, in_op[5]);
  not not_27 (not_27_out, in_op[4]);
  not not_28 (not_28_out, in_op[2]);
  and op_slti (op_slti_out, not_26_out, not_27_out, in_op[3], not_28_out, in_op[1], not_29_out);
  not not_29 (not_29_out, in_op[0]);
  not not_30 (not_30_out, in_op[5]);
  not not_31 (not_31_out, in_op[4]);
  not not_32 (not_32_out, in_op[2]);
  and op_sltiu (op_sltiu_out, not_30_out, not_31_out, in_op[3], not_32_out, in_op[1], in_op[0]);
  not not_33 (not_33_out, in_op[5]);
  not not_34 (not_34_out, in_op[4]);
  and op_lui (op_lui_out, not_33_out, not_34_out, in_op[3], in_op[2], in_op[1], in_op[0]);
  not not_35 (not_35_out, in_op[4]);
  not not_36 (not_36_out, in_op[3]);
  and lw (MemtoReg, in_op[5], not_35_out, not_36_out, not_37_out, in_op[1], in_op[0]);
  not not_37 (not_37_out, in_op[2]);
  not not_38 (not_38_out, in_op[4]);
  not not_39 (not_39_out, in_op[2]);
  and sw (MemWr, in_op[5], not_38_out, in_op[3], not_39_out, in_op[1], in_op[0]);
  not not_40 (not_40_out, in_op[5]);
  not not_41 (not_41_out, in_op[4]);
  not not_42 (not_42_out, in_op[3]);
  not not_43 (not_43_out, in_op[1]);
  and beq (beq_out, not_40_out, not_41_out, not_42_out, in_op[2], not_43_out, not_44_out);
  not not_44 (not_44_out, in_op[0]);
  not not_45 (not_45_out, in_op[5]);
  not not_46 (not_46_out, in_op[4]);
  not not_47 (not_47_out, in_op[3]);
  not not_48 (not_48_out, in_op[2]);
  not not_49 (not_49_out, in_op[0]);
  and op_j (Jump, not_45_out, not_46_out, not_47_out, not_48_out, in_op[1], not_49_out);
  not not_50 (not_50_out, in_op[5]);
  not not_51 (not_51_out, in_op[4]);
  not not_52 (not_52_out, in_op[3]);
  not not_53 (not_53_out, in_op[1]);
  and bne (Nzero, not_50_out, not_51_out, not_52_out, in_op[2], not_53_out, in_op[0]);
  or or_5 (or_5_out, MemWr, beq_out, Jump, Nzero);
  or or_6 (ALUsrc, op_xori_out, op_andi_out, ori_out, addiu_out, MemtoReg, MemWr, op_addi_out, op_slti_out, op_sltiu_out, op_lui_out);
  or or_7 (ExtOp, addiu_out, MemtoReg, MemWr, op_addi_out, op_slti_out);
  or or_8 (Branch, beq_out, Nzero);
  not not_54 (RegWr, or_5_out);

  assign Rtype = RegDst;

  // Notes on the sheet:
  //   1:rd, 0:rt
  //   1:imm, 0:bus
  //   1:sign, 0:zero (on imm)
endmodule

module adder32 (
  input  in_Cin,
  input  [31:0] in_A,
  input  [31:0] in_B,
  output [31:0] out_F,
  output out_SF,
  output out_CF,
  output out_ZF,
  output out_OF
);

  wire adder_1_cout, and_1_out, and_2_out, not_1_out, not_2_out, not_3_out;

  Adder #(.width(32)) adder_1 (.a(in_A), .b(in_B), .out(out_F), .cin(in_Cin), .cout(adder_1_cout));
  xor b (out_CF, in_Cin, adder_1_cout);
  nor32 c (.in32(out_F), .result(out_ZF));
  not not_1 (not_1_out, in_A[31]);
  not not_2 (not_2_out, in_B[31]);
  and and_1 (and_1_out, not_1_out, not_2_out, out_F[31]);
  and and_2 (and_2_out, in_A[31], in_B[31], not_3_out);
  not not_3 (not_3_out, out_F[31]);
  or or_1 (out_OF, and_1_out, and_2_out);

  assign out_SF = out_F[31];
endmodule

module nor32 (
  input  [31:0] in32,
  output result
);

  wire or_1_out;

  or or_1 (or_1_out, in32[0], in32[1], in32[2], in32[3], in32[4], in32[5], in32[6], in32[7], in32[8], in32[9], in32[10], in32[11], in32[12], in32[13], in32[14], in32[15], in32[16], in32[17], in32[18], in32[19], in32[20], in32[21], in32[22], in32[23], in32[24], in32[25], in32[26], in32[27], in32[28], in32[29], in32[30], in32[31]);
  not not_1 (result, or_1_out);
endmodule

module ALU (
  input  [31:0] in_A,
  input  [31:0] in_B,
  input  [4:0] ALUctr,
  input  [4:0] in_shamt,
  output out_Zero,
  output out_Overflow,
  output [31:0] out_Result
);

  wire Adder_out_cf, Adder_out_of, Adder_out_sf, multiplexer_3_p3, not_1_out, OVctl, SIGctl, SUBctl,
       xor_3_out;
  wire [3:0] OPcode;
  wire [4:0] multiplexer_1_out;
  wire [31:0] adder, and_out, bit_extender_1_out, nor_out, or_out, shift_left_16, sll_out, slt, sra_out,
       srl_out, xor_1_out, xor_out;

  assign or_out = in_A | in_B;  // OR_Gate or_1, 32 bits wide
  assign nor_out = ~(in_A | in_B);  // NOR_Gate nor_1, 32 bits wide
  Shifter #(.width(32)) shifter_1 (.in(in_B), .\dist (5'b10000), .out(shift_left_16));
  assign bit_extender_1_out = {{31{SUBctl}}, SUBctl};  // Bit_Extender bit_extender_1
  Multiplexer #(.width(5)) multiplexer_1 (.in0(in_shamt), .in1(in_A[4:0]), .out(multiplexer_1_out), .sel(SIGctl));
  ALU_dec ALU_decoder (.in_op(ALUctr), .SUB(SUBctl), .OV(OVctl), .SIG(SIGctl), .OP(OPcode));
  assign xor_1_out = in_B ^ bit_extender_1_out;  // XOR_Gate xor_1, 32 bits wide
  assign xor_out = in_A ^ in_B;  // XOR_Gate xor_2, 32 bits wide
  assign and_out = in_A & in_B;  // AND_Gate and_1, 32 bits wide
  Shifter #(.width(32)) shifter_2 (.in(in_B), .\dist (multiplexer_1_out), .out(sll_out));
  Shifter #(.shift("lr"), .width(32)) shifter_3 (.in(in_B), .\dist (multiplexer_1_out), .out(srl_out));
  Shifter #(.shift("ar"), .width(32)) shifter_4 (.in(in_B), .\dist (multiplexer_1_out), .out(sra_out));
  Multiplexer #(.select(4), .width(32)) multiplexer_2 (
    .in0(adder), .in1(or_out), .in2(slt), .in3(sll_out), .in4(srl_out), .in5(and_out), .in6(xor_out),
    .in7(shift_left_16), .in8(sra_out), .in9(nor_out), .out(out_Result), .sel(OPcode));  // open: in10, in11, in12, in13, in14, in15
  adder32 u_Adder (
    .in_Cin(SUBctl), .in_A(in_A), .in_B(xor_1_out), .out_F(adder), .out_SF(Adder_out_sf),
    .out_CF(Adder_out_cf), .out_ZF(out_Zero), .out_OF(Adder_out_of));
  not not_1 (not_1_out, Adder_out_cf);
  xor xor_3 (xor_3_out, Adder_out_sf, Adder_out_of);
  // Multiplexer #(.width(32)) multiplexer_3: pin names not known; wires that end beside it: {32{1'b0}}, 32'h1, multiplexer_3_p3, slt
  Multiplexer multiplexer_4 (.in0(not_1_out), .in1(xor_3_out), .out(multiplexer_3_p3), .sel(SIGctl));
  and and_2 (out_Overflow, Adder_out_of, OVctl);

  // Other names for the same wires on the sheet: inA[31:0] = in_A; inB[31:0] = in_B
endmodule

module ALU_dec (
  input  [4:0] in_op,
  output SUB,
  output OV,
  output SIG,
  output [3:0] OP
);

  wire decoder_1_out0, decoder_1_out1, decoder_1_out2, decoder_1_out3, decoder_1_out4, decoder_1_out5,
       decoder_1_out6, decoder_1_out7, decoder_1_out8, decoder_1_out9, decoder_1_out10, decoder_1_out11,
       decoder_1_out12, decoder_1_out13, decoder_1_out14, decoder_1_out15, decoder_1_out16;

  Decoder #(.select(5)) decoder_1 (
    .out0(decoder_1_out0), .out1(decoder_1_out1), .out2(decoder_1_out2), .out3(decoder_1_out3),
    .out4(decoder_1_out4), .out5(decoder_1_out5), .out6(decoder_1_out6), .out7(decoder_1_out7),
    .out8(decoder_1_out8), .out9(decoder_1_out9), .out10(decoder_1_out10), .out11(decoder_1_out11),
    .out12(decoder_1_out12), .out13(decoder_1_out13), .out14(decoder_1_out14), .out15(decoder_1_out15),
    .out16(decoder_1_out16), .sel(in_op));  // open: out17, out18, out19, out20, out21, out22, out23, out24, out25, out26, out27, out28, out29, out30, out31, en
  or or_1 (SUB, decoder_1_out4, decoder_1_out5, decoder_1_out6, decoder_1_out7);
  or or_2 (OV, decoder_1_out1, decoder_1_out5);
  or or_3 (SIG, decoder_1_out16, decoder_1_out15, decoder_1_out11, decoder_1_out7);
  or or_4 (OP[0], decoder_1_out2, decoder_1_out3, decoder_1_out9, decoder_1_out11, decoder_1_out12, decoder_1_out13);
  or or_5 (OP[1], decoder_1_out6, decoder_1_out7, decoder_1_out3, decoder_1_out10, decoder_1_out11, decoder_1_out12);
  or or_6 (OP[2], decoder_1_out8, decoder_1_out9, decoder_1_out10, decoder_1_out12, decoder_1_out8, decoder_1_out15);
  or or_7 (OP[3], decoder_1_out13, decoder_1_out14, decoder_1_out16);
endmodule

module reg32 (
  input  clear,
  input  [4:0] in_Ra,
  input  [4:0] in_Rb,
  input  [4:0] in_Rw,
  input  in_WE,
  input  [31:0] in_Rwdata,
  input  clk,
  output [31:0] out_Ra,
  output [31:0] out_Rb
);

  wire decoder_1_out0, decoder_1_out1, decoder_1_out2, decoder_1_out3;
  wire [31:0] reg8_0locked_1_out_r1data, reg8_0locked_1_out_r2data, reg8_1_out_r1data, reg8_1_out_r2data,
       reg8_2_out_r1data, reg8_2_out_r2data, reg8_3_out_r1data, reg8_3_out_r2data;

  Decoder #(.select(2)) decoder_1 (
    .out0(decoder_1_out0), .out1(decoder_1_out1), .out2(decoder_1_out2), .out3(decoder_1_out3),
    .sel(in_Rw[4:3]), .en(in_WE));
  reg8_0locked reg8_0locked_1 (
    .in_Rwdata(in_Rwdata), .clk(clk), .in_WE(decoder_1_out0), .in_Rwaddr(in_Rw[2:0]), .clear(clear),
    .in_R1addr(in_Ra[2:0]), .in_R2addr(in_Rb[2:0]), .out_R1data(reg8_0locked_1_out_r1data),
    .out_R2data(reg8_0locked_1_out_r2data));
  reg8 reg8_1 (
    .in_Rwdata(in_Rwdata), .clk(clk), .in_WE(decoder_1_out1), .in_Rwaddr(in_Rw[2:0]), .clear(clear),
    .in_R1addr(in_Ra[2:0]), .in_R2addr(in_Rb[2:0]), .out_R1data(reg8_1_out_r1data),
    .out_R2data(reg8_1_out_r2data));
  reg8 reg8_2 (
    .in_Rwdata(in_Rwdata), .clk(clk), .in_WE(decoder_1_out2), .in_Rwaddr(in_Rw[2:0]), .clear(clear),
    .in_R1addr(in_Ra[2:0]), .in_R2addr(in_Rb[2:0]), .out_R1data(reg8_2_out_r1data),
    .out_R2data(reg8_2_out_r2data));
  reg8 reg8_3 (
    .in_Rwdata(in_Rwdata), .clk(clk), .in_WE(decoder_1_out3), .in_Rwaddr(in_Rw[2:0]), .clear(clear),
    .in_R1addr(in_Ra[2:0]), .in_R2addr(in_Rb[2:0]), .out_R1data(reg8_3_out_r1data),
    .out_R2data(reg8_3_out_r2data));
  Multiplexer #(.select(2), .width(32)) multiplexer_1 (
    .in0(reg8_0locked_1_out_r1data), .in1(reg8_1_out_r1data), .in2(reg8_2_out_r1data),
    .in3(reg8_3_out_r1data), .out(out_Ra), .sel(in_Ra[4:3]));
  Multiplexer #(.select(2), .width(32)) multiplexer_2 (
    .in0(reg8_0locked_1_out_r2data), .in1(reg8_1_out_r2data), .in2(reg8_2_out_r2data),
    .in3(reg8_3_out_r2data), .out(out_Rb), .sel(in_Rb[4:3]));
endmodule

module reg8 (
  input  [31:0] in_Rwdata,
  input  clk,
  input  in_WE,
  input  [2:0] in_Rwaddr,
  input  clear,
  input  [2:0] in_R1addr,
  input  [2:0] in_R2addr,
  output [31:0] out_R1data,
  output [31:0] out_R2data
);

  wire decoder_1_out0, decoder_1_out1, decoder_1_out2, decoder_1_out3, decoder_1_out4, decoder_1_out5,
       decoder_1_out6, decoder_1_out7;
  wire [31:0] reg0_q, reg1_q, reg2_q, reg3_q, reg4_q, reg5_q, reg6_q, reg7_q;

  Decoder #(.select(3)) decoder_1 (
    .out0(decoder_1_out0), .out1(decoder_1_out1), .out2(decoder_1_out2), .out3(decoder_1_out3),
    .out4(decoder_1_out4), .out5(decoder_1_out5), .out6(decoder_1_out6), .out7(decoder_1_out7),
    .sel(in_Rwaddr), .en(in_WE));
  Register #(.trigger("falling"), .width(32)) reg0 (
    .D(in_Rwdata), .en(decoder_1_out0), .clk(clk), .Q(reg0_q), .clr(clear));
  Register #(.trigger("falling"), .width(32)) reg1 (
    .D(in_Rwdata), .en(decoder_1_out1), .clk(clk), .Q(reg1_q), .clr(clear));
  Register #(.trigger("falling"), .width(32)) reg2 (
    .D(in_Rwdata), .en(decoder_1_out2), .clk(clk), .Q(reg2_q), .clr(clear));
  Register #(.trigger("falling"), .width(32)) reg3 (
    .D(in_Rwdata), .en(decoder_1_out3), .clk(clk), .Q(reg3_q), .clr(clear));
  Register #(.trigger("falling"), .width(32)) reg4 (
    .D(in_Rwdata), .en(decoder_1_out4), .clk(clk), .Q(reg4_q), .clr(clear));
  Register #(.trigger("falling"), .width(32)) reg5 (
    .D(in_Rwdata), .en(decoder_1_out5), .clk(clk), .Q(reg5_q), .clr(clear));
  Register #(.trigger("falling"), .width(32)) reg6 (
    .D(in_Rwdata), .en(decoder_1_out6), .clk(clk), .Q(reg6_q), .clr(clear));
  Register #(.trigger("falling"), .width(32)) reg7 (
    .D(in_Rwdata), .en(decoder_1_out7), .clk(clk), .Q(reg7_q), .clr(clear));
  Multiplexer #(.select(3), .width(32)) multiplexer_1 (
    .in0(reg0_q), .in1(reg1_q), .in2(reg2_q), .in3(reg3_q), .in4(reg4_q), .in5(reg5_q), .in6(reg6_q),
    .in7(reg7_q), .out(out_R1data), .sel(in_R1addr));
  Multiplexer #(.select(3), .width(32)) multiplexer_2 (
    .in0(reg0_q), .in1(reg1_q), .in2(reg2_q), .in3(reg3_q), .in4(reg4_q), .in5(reg5_q), .in6(reg6_q),
    .in7(reg7_q), .out(out_R2data), .sel(in_R2addr));
endmodule

module reg8_0locked (
  input  [31:0] in_Rwdata,
  input  clk,
  input  in_WE,
  input  [2:0] in_Rwaddr,
  input  clear,
  input  [2:0] in_R1addr,
  input  [2:0] in_R2addr,
  output [31:0] out_R1data,
  output [31:0] out_R2data
);

  wire decoder_1_out1, decoder_1_out2, decoder_1_out3, decoder_1_out4, decoder_1_out5, decoder_1_out6,
       decoder_1_out7;
  wire [31:0] reg0_q, reg1_q, reg2_q, reg3_q, reg4_q, reg5_q, reg6_q, reg7_q;

  Decoder #(.select(3)) decoder_1 (
    .out1(decoder_1_out1), .out2(decoder_1_out2), .out3(decoder_1_out3), .out4(decoder_1_out4),
    .out5(decoder_1_out5), .out6(decoder_1_out6), .out7(decoder_1_out7), .sel(in_Rwaddr), .en(in_WE));  // open: out0
  Register #(.trigger("falling"), .width(32)) reg0 (.clk(clk), .Q(reg0_q), .clr(1'b1));  // open: D, en
  Register #(.trigger("falling"), .width(32)) reg1 (
    .D(in_Rwdata), .en(decoder_1_out1), .clk(clk), .Q(reg1_q), .clr(clear));
  Register #(.trigger("falling"), .width(32)) reg2 (
    .D(in_Rwdata), .en(decoder_1_out2), .clk(clk), .Q(reg2_q), .clr(clear));
  Register #(.trigger("falling"), .width(32)) reg3 (
    .D(in_Rwdata), .en(decoder_1_out3), .clk(clk), .Q(reg3_q), .clr(clear));
  Register #(.trigger("falling"), .width(32)) reg4 (
    .D(in_Rwdata), .en(decoder_1_out4), .clk(clk), .Q(reg4_q), .clr(clear));
  Register #(.trigger("falling"), .width(32)) reg5 (
    .D(in_Rwdata), .en(decoder_1_out5), .clk(clk), .Q(reg5_q), .clr(clear));
  Register #(.trigger("falling"), .width(32)) reg6 (
    .D(in_Rwdata), .en(decoder_1_out6), .clk(clk), .Q(reg6_q), .clr(clear));
  Register #(.trigger("falling"), .width(32)) reg7 (
    .D(in_Rwdata), .en(decoder_1_out7), .clk(clk), .Q(reg7_q), .clr(clear));
  Multiplexer #(.select(3), .width(32)) multiplexer_1 (
    .in0(reg0_q), .in1(reg1_q), .in2(reg2_q), .in3(reg3_q), .in4(reg4_q), .in5(reg5_q), .in6(reg6_q),
    .in7(reg7_q), .out(out_R1data), .sel(in_R1addr));
  Multiplexer #(.select(3), .width(32)) multiplexer_2 (
    .in0(reg0_q), .in1(reg1_q), .in2(reg2_q), .in3(reg3_q), .in4(reg4_q), .in5(reg5_q), .in6(reg6_q),
    .in7(reg7_q), .out(out_R2data), .sel(in_R2addr));
endmodule

module ext_mux (
  input  [15:0] in_16,
  input  ext_op,
  output [31:0] out_32
);

  wire [31:0] bit_extender_1_out, bit_extender_2_out;

  assign bit_extender_1_out = {{16{1'b0}}, in_16};  // Bit_Extender bit_extender_1
  assign bit_extender_2_out = {{16{in_16[15]}}, in_16};  // Bit_Extender bit_extender_2
  Multiplexer #(.width(32)) multiplexer_1 (
    .in0(bit_extender_1_out), .in1(bit_extender_2_out), .out(out_32), .sel(ext_op));
endmodule

module branch_predictor (
  input  result,
  input  WE,
  input  clk,
  input  clr,
  output prediction
);

  wire and_1_out;
  wire [0:0] register_1_q;
  wire [1:1] multiplexer_1_out;

  Register #(.trigger("falling"), .width(2)) register_1 (
    .D({multiplexer_1_out[1], result}), .en(WE), .clk(clk), .Q({prediction, register_1_q[0]}), .clr(clr));
  Multiplexer multiplexer_1 (.in0(prediction), .in1(result), .out(multiplexer_1_out[1]), .sel(and_1_out));
  and and_1 (and_1_out, result, register_1_q[0]);
endmodule
